// Logisim project R-PRHD.circ as structural Verilog: 13 circuits, main circuit main
module main (
  input  CLR_AR,
  input  CLR_PC,
  input  CLR_DR,
  input  CLR_TR,
  input  INC_TR,
  input  LD_TR,
  input  LD_OP
);

  wire CLK, CLR_AC, decoder_1_out0, decoder_1_out1, decoder_1_out2, decoder_1_out3, decoder_1_out4,
       decoder_1_out5, decoder_1_out6, decoder_1_out7, decoder_2_out0, decoder_2_out1, decoder_2_out2,
       decoder_2_out3, decoder_2_out4, decoder_2_out5, decoder_2_out6, decoder_2_out7, E, E_CLR, E_COM, E_LD,
       INC_AC, INC_AR, INC_DR, INC_PC, LD_AC, LD_AR, LD_DR, LD_IR, LD_PC, timing_control_1_w_en;
  wire [2:0] ALU_SEL, BUS_SEL, OPCODE, T_S;
  wire [11:0] AR_12;
  wire [15:0] D_AC, D_AR, D_DR, D_IR, D_PC, D_TR, RAM_IN, RAM_OP;

  // Probe on BUS_SEL
  Clock clock_1 (.out(CLK));
  Decoder #(.enable("false"), .select(3)) decoder_1 (
    .out0(decoder_1_out0), .out1(decoder_1_out1), .out2(decoder_1_out2), .out3(decoder_1_out3),
    .out4(decoder_1_out4), .out5(decoder_1_out5), .out6(decoder_1_out6), .out7(decoder_1_out7), .sel(OPCODE));
  LED led_1 (.in(decoder_1_out0));
  LED led_2 (.in(decoder_1_out1));
  LED led_3 (.in(decoder_1_out2));
  LED led_4 (.in(decoder_1_out3));
  LED led_5 (.in(decoder_1_out4));
  LED led_6 (.in(decoder_1_out5));
  LED led_7 (.in(decoder_1_out6));
  LED led_8 (.in(decoder_1_out7));
  // Probe on D_DR
  // Probe on D_AC
  // Probe on D_IR
  // Probe on D_TR
  DATAPATH datapath_1 (
    .CLK(CLK), .CLR_AR(CLR_AR), .INC_AR(INC_AR), .LD_EN_AR(LD_AR), .CLR_PC(CLR_PC), .INC_PC(INC_PC),
    .LD_EN_PC(LD_PC), .CLR_DR(CLR_DR), .INC_DR(INC_DR), .LD_EN_DR(LD_DR), .CLR_AC(CLR_AC), .INC_AC(INC_AC),
    .LD_EN_AC(LD_AC), .ALU_sel(ALU_SEL), .MEMORY_IP(RAM_OP), .IR_ld_en(LD_IR), .SELCTION_LINE(BUS_SEL),
    .CLR_TR(CLR_TR), .INC_TR(INC_TR), .LD_EN_TR(LD_TR), .LD_EN_op(LD_OP), .COMP_E(E_COM), .CLR_E(E_CLR),
    .LOAD_EN_E(E_LD), .AR_OUT(D_AR), .BIT_12_AR(AR_12), .PC_OUT(D_PC), .DR_OUT(D_DR), .AC_OUT(D_AC),
    .IR_OUT(D_IR), .TR_OUT(D_TR), .MEMORY_OP(RAM_IN), .E(E));  // open: OUTR_OUT
  Decoder #(.enable("false"), .select(3)) decoder_2 (
    .out0(decoder_2_out0), .out1(decoder_2_out1), .out2(decoder_2_out2), .out3(decoder_2_out3),
    .out4(decoder_2_out4), .out5(decoder_2_out5), .out6(decoder_2_out6), .out7(decoder_2_out7), .sel(T_S));
  LED led_9 (.in(decoder_2_out0));
  LED led_10 (.in(decoder_2_out1));
  LED led_11 (.in(decoder_2_out2));
  LED led_12 (.in(decoder_2_out3));
  LED led_13 (.in(decoder_2_out4));
  LED led_14 (.in(decoder_2_out5));
  LED led_15 (.in(decoder_2_out6));
  LED led_16 (.in(decoder_2_out7));
  // Probe on D_PC
  // Probe on D_AR
  TIMING_CONTROL timing_control_1 (
    .IR_OP(D_IR), .CLK(CLK), .AC(D_AC), .DR(D_DR), .E(E), .OPCODE(OPCODE), .T_S(T_S), .Load_AR(LD_AR),
    .INR_AR(INC_AR), .IR_Load(LD_IR), .LD_PC(LD_PC), .Ld_dr(LD_DR), .INR_PC(INC_PC), .INC_DR(INC_DR),
    .INC_AC(INC_AC), .CLR_AC(CLR_AC), .LD_AC(LD_AC), .ALU_SEL(ALU_SEL), .BUS_SEL(BUS_SEL),
    .W_EN(timing_control_1_w_en), .E_COM(E_COM), .E_CLR(E_CLR), .E_LOAD(E_LD));
  RAM #(.addrWidth(12), .dataWidth(16), .enables("line")) ram_1 (
    .addr(AR_12), .we(timing_control_1_w_en), .clk(CLK), .din(RAM_IN), .dout(RAM_OP));
  // Probe on RAM_OP

  // Notes on the sheet:
  //   and
  //   add
  //   lda
  //   sta
  //   bun
  //   bsa
  //   isz
  //   T0
  //   T1
  //   T2
  //   T3
  //   T4
  //   T5
  //   T6
  //   T7
endmodule

module AR (
  input  clr,
  input  INR,
  input  [15:0] DATAIN,
  input  LOAD,
  input  clk,
  output [15:0] AR_op,
  output [11:0] BIT_12_OP
);

  wire [11:0] adder_1_out, multiplexer_1_out, multiplexer_2_out, multiplexer_3_out;

  Multiplexer #(.width(12)) multiplexer_1 (.in0(AR_op[11:0]), .in1({12{1'b0}}), .out(multiplexer_1_out), .sel(clr));
  Adder #(.width(12)) adder_1 (.a(AR_op[11:0]), .b(12'h1), .out(adder_1_out), .cin(1'b0));  // open: cout
  Multiplexer #(.width(12)) multiplexer_2 (
    .in0(multiplexer_1_out), .in1(adder_1_out), .out(multiplexer_2_out), .sel(INR));
  Multiplexer #(.width(12)) multiplexer_3 (
    .in0(multiplexer_2_out), .in1(DATAIN[11:0]), .out(multiplexer_3_out), .sel(LOAD));
  Register #(.width(12)) register_1 (.D(multiplexer_3_out), .clk(clk), .Q(AR_op[11:0]));  // open: en, clr

  assign AR_op[15:12] = 4'b0000;
  assign BIT_12_OP = AR_op[11:0];

  // Other names for the same wires on the sheet: Q[11:0] = AR_op[11:0]
endmodule

module PC (
  input  clr,
  input  INR,
  input  [15:0] DATAIN,
  input  LOAD,
  input  clk,
  output [15:0] PC_op,
  output [11:0] BIT_12_OP
);

  wire [11:0] adder_1_out, multiplexer_1_out, multiplexer_2_out, multiplexer_3_out;

  Multiplexer #(.width(12)) multiplexer_1 (.in0(BIT_12_OP), .in1({12{1'b0}}), .out(multiplexer_1_out), .sel(clr));
  Adder #(.width(12)) adder_1 (.a(BIT_12_OP), .b(12'h1), .out(adder_1_out), .cin(1'b0));  // open: cout
  Multiplexer #(.width(12)) multiplexer_2 (
    .in0(multiplexer_1_out), .in1(adder_1_out), .out(multiplexer_2_out), .sel(INR));
  Multiplexer #(.width(12)) multiplexer_3 (
    .in0(multiplexer_2_out), .in1(DATAIN[11:0]), .out(multiplexer_3_out), .sel(LOAD));
  Register #(.width(12)) register_1 (.D(multiplexer_3_out), .clk(clk), .Q(BIT_12_OP));  // open: en, clr

  assign PC_op = {4'b0000, BIT_12_OP};

  // Other names for the same wires on the sheet: Q[11:0] = BIT_12_OP
endmodule

module DR (
  input  clr,
  input  [15:0] DATAIN,
  input  INR,
  input  LOAD,
  input  clk,
  output [15:0] DR_op
);

  wire [15:0] adder_1_out, multiplexer_1_out, multiplexer_2_out, multiplexer_3_out;

  Multiplexer #(.width(16)) multiplexer_1 (.in0(DR_op), .in1({16{1'b0}}), .out(multiplexer_1_out), .sel(clr));
  Adder #(.width(16)) adder_1 (.a(DR_op), .b(16'h1), .out(adder_1_out), .cin(1'b0));  // open: cout
  Multiplexer #(.width(16)) multiplexer_2 (
    .in0(multiplexer_1_out), .in1(adder_1_out), .out(multiplexer_2_out), .sel(INR));
  Multiplexer #(.width(16)) multiplexer_3 (.in0(multiplexer_2_out), .in1(DATAIN), .out(multiplexer_3_out), .sel(LOAD));
  Register #(.width(16)) register_1 (.D(multiplexer_3_out), .clk(clk), .Q(DR_op));  // open: en, clr

  // Other names for the same wires on the sheet: Q[15:0] = DR_op
endmodule

module AC (
  input  clr,
  input  [15:0] DATAIN,
  input  INR,
  input  LOAD,
  input  clk,
  output [15:0] AC_op
);

  wire [15:0] adder_1_out, multiplexer_1_out, multiplexer_2_out, multiplexer_3_out;

  Multiplexer #(.width(16)) multiplexer_1 (.in0(AC_op), .in1({16{1'b0}}), .out(multiplexer_1_out), .sel(clr));
  Adder #(.width(16)) adder_1 (.a(AC_op), .b(16'h1), .out(adder_1_out), .cin(1'b0));  // open: cout
  Multiplexer #(.width(16)) multiplexer_2 (
    .in0(multiplexer_1_out), .in1(adder_1_out), .out(multiplexer_2_out), .sel(INR));
  Multiplexer #(.width(16)) multiplexer_3 (.in0(multiplexer_2_out), .in1(DATAIN), .out(multiplexer_3_out), .sel(LOAD));
  Register #(.width(16)) register_1 (.D(multiplexer_3_out), .clk(clk), .Q(AC_op));  // open: en, clr

  // Other names for the same wires on the sheet: Q[15:0] = AC_op
endmodule

module IR (
  input  clr,
  input  [15:0] DATAIN,
  input  INR,
  input  LOAD,
  input  clk,
  output [15:0] IR_op
);

  wire [15:0] adder_1_out, multiplexer_1_out, multiplexer_2_out, multiplexer_3_out;

  Multiplexer #(.width(16)) multiplexer_1 (.in0(IR_op), .in1({16{1'b0}}), .out(multiplexer_1_out), .sel(clr));
  Adder #(.width(16)) adder_1 (.a(IR_op), .b(16'h1), .out(adder_1_out), .cin(1'b0));  // open: cout
  Multiplexer #(.width(16)) multiplexer_2 (
    .in0(multiplexer_1_out), .in1(adder_1_out), .out(multiplexer_2_out), .sel(INR));
  Multiplexer #(.width(16)) multiplexer_3 (.in0(multiplexer_2_out), .in1(DATAIN), .out(multiplexer_3_out), .sel(LOAD));
  Register #(.width(16)) register_1 (.D(multiplexer_3_out), .clk(clk), .Q(IR_op));  // open: en, clr

  // Other names for the same wires on the sheet: Q[15:0] = IR_op
endmodule

module TR (
  input  clr,
  input  [15:0] DATAIN,
  input  INR,
  input  LOAD,
  input  clk,
  output [15:0] TR_op
);

  wire [15:0] adder_1_out, multiplexer_1_out, multiplexer_2_out, multiplexer_3_out;

  Multiplexer #(.width(16)) multiplexer_1 (.in0(TR_op), .in1({16{1'b0}}), .out(multiplexer_1_out), .sel(clr));
  Adder #(.width(16)) adder_1 (.a(TR_op), .b(16'h1), .out(adder_1_out), .cin(1'b0));  // open: cout
  Multiplexer #(.width(16)) multiplexer_2 (
    .in0(multiplexer_1_out), .in1(adder_1_out), .out(multiplexer_2_out), .sel(INR));
  Multiplexer #(.width(16)) multiplexer_3 (.in0(multiplexer_2_out), .in1(DATAIN), .out(multiplexer_3_out), .sel(LOAD));
  Register #(.width(16)) register_1 (.D(multiplexer_3_out), .clk(clk), .Q(TR_op));  // open: en, clr

  // Other names for the same wires on the sheet: Q[15:0] = TR_op
endmodule

module OUTR (
  input  clr,
  input  inc,
  input  [15:0] load,
  input  Ld_en,
  input  clk,
  output [15:0] op
);

  wire [7:0] adder_1_out, multiplexer_1_out, multiplexer_2_out, multiplexer_3_out;

  Multiplexer #(.width(8)) multiplexer_1 (.in0(op[7:0]), .in1({8{1'b0}}), .out(multiplexer_1_out), .sel(clr));
  Adder adder_1 (.a(op[7:0]), .b(8'h1), .out(adder_1_out), .cin(1'b0));  // open: cout
  Multiplexer #(.width(8)) multiplexer_2 (
    .in0(multiplexer_1_out), .in1(adder_1_out), .out(multiplexer_2_out), .sel(inc));
  Multiplexer #(.width(8)) multiplexer_3 (
    .in0(multiplexer_2_out), .in1(load[7:0]), .out(multiplexer_3_out), .sel(Ld_en));
  Register register_1 (.D(multiplexer_3_out), .clk(clk), .Q(op[7:0]));  // open: en, clr

  assign op[15:8] = {8{1'b0}};

  // Other names for the same wires on the sheet: Q[7:0] = op[7:0]
endmodule

module ALU (
  input  [15:0] AC,
  input  [15:0] DR,
  input  [15:0] INPR,
  input  [2:0] ALU_sel,
  output [15:0] Alu_out,
  output Cout
);

  wire [15:0] adder_1_out, and_1_out, not_1_out;

  assign not_1_out = ~AC;  // NOT_Gate not_1, 16 bits wide
  Adder #(.width(16)) adder_1 (.a(AC), .b(DR), .out(adder_1_out), .cin(1'b0), .cout(Cout));
  assign and_1_out = AC & DR;  // AND_Gate and_1, 16 bits wide
  Multiplexer #(.select(3), .width(16)) multiplexer_1 (
    .in0(and_1_out), .in1(adder_1_out), .in2(DR), .in3(INPR), .in4(not_1_out), .in5({AC[0], AC[15:1]}),
    .in6({AC[14:0], AC[15]}), .out(Alu_out), .sel(ALU_sel));  // open: in7
endmodule

module E_FF (
  input  DATAIN,
  input  E_COMP,
  input  CLR,
  input  CLK,
  input  LOAD,
  output E
);

  wire multiplexer_1_out, multiplexer_2_out, multiplexer_3_out, not_1_out;

  not not_1 (not_1_out, E);
  Multiplexer multiplexer_1 (.in0(E), .in1(not_1_out), .out(multiplexer_1_out), .sel(E_COMP));
  Multiplexer multiplexer_2 (.in0(multiplexer_1_out), .in1(1'b0), .out(multiplexer_2_out), .sel(CLR));
  Multiplexer multiplexer_3 (.in0(multiplexer_2_out), .in1(DATAIN), .out(multiplexer_3_out), .sel(LOAD));
  D_Flip_Flop d_ff_1 (.D(multiplexer_3_out), .clk(CLK), .Q(E));  // open: Qn, preset, reset
endmodule

module DATAPATH (
  input  CLK,
  input  CLR_AR,
  input  INC_AR,
  input  LD_EN_AR,
  input  CLR_PC,
  input  INC_PC,
  input  LD_EN_PC,
  input  CLR_DR,
  input  INC_DR,
  input  LD_EN_DR,
  input  CLR_AC,
  input  INC_AC,
  input  LD_EN_AC,
  input  [2:0] ALU_sel,
  input  [15:0] MEMORY_IP,
  input  IR_ld_en,
  input  [2:0] SELCTION_LINE,
  input  CLR_TR,
  input  INC_TR,
  input  LD_EN_TR,
  input  LD_EN_op,
  input  COMP_E,
  input  CLR_E,
  input  LOAD_EN_E,
  output [15:0] AR_OUT,
  output [11:0] BIT_12_AR,
  output [15:0] PC_OUT,
  output [15:0] DR_OUT,
  output [15:0] AC_OUT,
  output [15:0] IR_OUT,
  output [15:0] TR_OUT,
  output [15:0] OUTR_OUT,
  output [15:0] MEMORY_OP,
  output E
);

  wire alu_1_cout;
  wire [15:0] alu_1_alu_out;

  ALU alu_1 (.AC(AC_OUT), .DR(DR_OUT), .ALU_sel(ALU_sel), .Alu_out(alu_1_alu_out), .Cout(alu_1_cout));  // open: INPR
  AR ar_1 (
    .clr(CLR_AR), .INR(INC_AR), .DATAIN(MEMORY_OP), .LOAD(LD_EN_AR), .clk(CLK), .AR_op(AR_OUT),
    .BIT_12_OP(BIT_12_AR));
  PC pc_1 (
    .clr(CLR_PC), .INR(INC_PC), .DATAIN(MEMORY_OP), .LOAD(LD_EN_PC), .clk(CLK), .PC_op(PC_OUT));  // open: BIT_12_OP
  DR dr_1 (.clr(CLR_DR), .DATAIN(MEMORY_OP), .INR(INC_DR), .LOAD(LD_EN_DR), .clk(CLK), .DR_op(DR_OUT));
  AC ac_1 (.clr(CLR_AC), .DATAIN(alu_1_alu_out), .INR(INC_AC), .LOAD(LD_EN_AC), .clk(CLK), .AC_op(AC_OUT));
  IR ir_1 (.clr(1'b0), .DATAIN(MEMORY_OP), .INR(1'b0), .LOAD(IR_ld_en), .clk(CLK), .IR_op(IR_OUT));
  TR tr_1 (.clr(CLR_TR), .DATAIN(MEMORY_OP), .INR(INC_TR), .LOAD(LD_EN_TR), .clk(CLK), .TR_op(TR_OUT));
  OUTR outr_1 (.clr(1'b0), .inc(1'b0), .load(MEMORY_OP), .Ld_en(LD_EN_op), .clk(CLK), .op(OUTR_OUT));
  E_FF e_ff_1 (.DATAIN(alu_1_cout), .E_COMP(COMP_E), .CLR(CLR_E), .CLK(CLK), .LOAD(LOAD_EN_E), .E(E));
  Multiplexer #(.select(3), .width(16)) multiplexer_1 (
    .in1(AR_OUT), .in2(PC_OUT), .in3(DR_OUT), .in4(AC_OUT), .in5(IR_OUT), .in6(TR_OUT), .in7(MEMORY_IP),
    .out(MEMORY_OP), .sel(SELCTION_LINE));  // open: in0
endmodule

module TIMING_CONTROL (
  input  [15:0] IR_OP,
  input  CLK,
  input  [15:0] AC,
  input  [15:0] DR,
  input  E,
  output [2:0] OPCODE,
  output [2:0] T_S,
  output Load_AR,
  output INR_AR,
  output IR_Load,
  output LD_PC,
  output Ld_dr,
  output INR_PC,
  output INC_DR,
  output INC_AC,
  output CLR_AC,
  output LD_AC,
  output [2:0] ALU_SEL,
  output [2:0] BUS_SEL,
  output W_EN,
  output E_COM,
  output E_CLR,
  output E_LOAD
);

  wire AC_not, and_1_out, and_2_out, and_3_out, and_4_out, and_5_out, and_6_out, and_7_out, and_8_out,
       and_9_out, and_10_out, and_11_out, and_12_out, and_13_out, and_14_out, and_15_out, and_16_out,
       and_17_out, and_18_out, and_19_out, and_20_out, and_25_out, and_26_out, and_27_out, and_28_out,
       and_29_out, and_30_out, and_31_out, and_32_out, and_33_out, and_36_out, and_37_out, and_38_out,
       and_39_out, and_40_out, and_42_out, and_43_out, and_44_out, and_45_out, CLR_SC, D0, D1, D2, D3, D4,
       D5, D6, D7, DR_not, ID7_0T3, not_1_out, not_2_out, not_3_out, or_1_out, or_2_out, or_3_out, or_4_out,
       or_5_out, or_13_out, or_17_out, or_18_out, or_19_out, or_20_out, or_24_out, p, r, T0, T2, T3, T4, T5,
       T6, T7;

  or or_1 (or_1_out, D0, D1, D2, D5);
  or or_2 (or_2_out, D3, D4);
  and and_1 (and_1_out, D1, T5);
  and and_2 (and_2_out, r, IR_OP[6]);
  and and_3 (and_3_out, r, IR_OP[7]);
  Decoder #(.select(3)) decoder_1 (
    .out0(D0), .out1(D1), .out2(D2), .out3(D3), .out4(D4), .out5(D5), .out6(D6), .out7(D7), .sel(IR_OP[14:12]));  // open: en
  or or_3 (or_3_out, D0, D1, D2);
  or or_4 (or_4_out, D0, D1, D2, D4, D6);
  or or_5 (or_5_out, D0, D1, D5, D2);
  and and_4 (and_4_out, or_1_out, T5);
  and and_5 (and_5_out, or_2_out, T4);
  and and_6 (and_6_out, D6, T6);
  and and_7 (and_7_out, T4, D4);
  and and_8 (and_8_out, T5, D5);
  and and_9 (and_9_out, or_3_out, T5);
  and and_10 (and_10_out, r, IR_OP[7]);
  and and_11 (and_11_out, r, IR_OP[6]);
  and and_12 (and_12_out, p, IR_OP[11]);
  and and_13 (and_13_out, or_4_out, T4);
  and and_14 (and_14_out, or_5_out, T5);
  or or_6 (E_LOAD, and_1_out, and_2_out, and_3_out);
  or or_7 (LD_PC, and_7_out, and_8_out);
  and and_15 (and_15_out, D1, T5);
  and and_16 (and_16_out, p, IR_OP[11]);
  and and_17 (and_17_out, r, IR_OP[7]);
  and and_18 (and_18_out, D6, T6);
  or or_8 (CLR_SC, and_4_out, r, and_5_out, p, and_6_out);
  and and_19 (and_19_out, r, T3);
  and and_20 (and_20_out, r, IR_OP[9]);
  or or_9 (ALU_SEL[0], and_15_out, and_16_out, and_17_out);
  or or_10 (BUS_SEL[0], IR_Load, ID7_0T3, T2, and_13_out, and_14_out, and_18_out);
  or or_11 (LD_AC, and_9_out, and_10_out, and_20_out, and_11_out, and_12_out);
  not not_1 (not_1_out, IR_OP[15]);
  not not_2 (not_2_out, D7);
  or or_12 (Load_AR, T0, T2, and_19_out);
  Decoder #(.select(3)) decoder_2 (
    .out0(T0), .out1(IR_Load), .out2(T2), .out3(T3), .out4(T4), .out5(T5), .out6(T6), .out7(T7), .sel(T_S));  // open: en
  and and_21 (r, not_1_out, D7, T3);
  and and_22 (p, IR_OP[15], D7, T3);
  and and_23 (ID7_0T3, IR_OP[15], not_2_out, T3);
  not not_3 (not_3_out, AC[15]);
  and and_24 (INC_AC, r, IR_OP[5]);
  or or_13 (or_13_out, D0, D1, D3, D2, D6);
  and and_25 (and_25_out, D6, DR_not, T6);
  and and_26 (and_26_out, not_3_out, r, IR_OP[4]);
  and and_27 (and_27_out, AC[15], r, IR_OP[4]);
  and and_28 (and_28_out, AC_not, r, IR_OP[2]);
  and and_29 (and_29_out, E, r, IR_OP[1]);
  and and_30 (and_30_out, D2, T5);
  and and_31 (and_31_out, p, IR_OP[11]);
  and and_32 (and_32_out, r, IR_OP[6]);
  and and_33 (and_33_out, or_13_out, T4);
  or or_14 (ALU_SEL[1], and_30_out, and_31_out, and_32_out);
  or or_15 (BUS_SEL[2], and_33_out, IR_Load, T2, ID7_0T3);
  and and_34 (E_CLR, r, IR_OP[10]);
  and and_35 (INR_AR, T4, D5);
  or or_16 (INR_PC, and_25_out, IR_Load, and_26_out, and_27_out, and_28_out, and_29_out);
  or or_17 (or_17_out, D0, D1, D5, D2, D6);
  or or_18 (or_18_out, D0, D1, D2);
  SEQUNCE_COUNTER sequnce_counter_1 (.CLK(CLK), .CLR(CLR_SC), .OP(T_S));
  or or_19 (or_19_out, AC[15], AC[14], AC[13], AC[12], AC[11], AC[10], AC[9], AC[8], AC[6], AC[5], AC[4], AC[3], AC[2], AC[1], AC[0], AC[7]);
  not not_4 (AC_not, or_19_out);
  and and_36 (and_36_out, or_17_out, T4);
  and and_37 (and_37_out, D6, T6);
  and and_38 (and_38_out, D3, T4);
  and and_39 (and_39_out, D5, T4);
  and and_40 (and_40_out, D6, T6);
  and and_41 (CLR_AC, r, IR_OP[11]);
  and and_42 (and_42_out, or_18_out, T5);
  and and_43 (and_43_out, r, IR_OP[9]);
  and and_44 (and_44_out, r, IR_OP[6]);
  and and_45 (and_45_out, r, IR_OP[7]);
  or or_20 (or_20_out, D0, D1, D2, D6);
  and and_46 (INC_DR, D6, T5);
  or or_21 (ALU_SEL[2], and_43_out, and_44_out, and_45_out);
  or or_22 (BUS_SEL[1], and_36_out, and_37_out, and_42_out, T0, IR_Load, ID7_0T3);
  or or_23 (W_EN, and_38_out, and_39_out, and_40_out);
  or or_24 (or_24_out, DR[15], DR[14], DR[13], DR[12], DR[11], DR[10], DR[9], DR[8], DR[6], DR[5], DR[4], DR[3], DR[2], DR[1], DR[0], DR[7]);
  not not_5 (DR_not, or_24_out);
  and and_47 (Ld_dr, or_20_out, T4);
  and and_48 (E_COM, r, IR_OP[8]);

  assign OPCODE = IR_OP[14:12];

  // Other names for the same wires on the sheet: AC_15 = AC[15]; S0 = ALU_SEL[0]; S1 = ALU_SEL[1]; S2 = ALU_SEL[2];
  //   S0_bus = BUS_SEL[0]; S1_bus = BUS_SEL[1]; S2_bus = BUS_SEL[2]; B0 = IR_OP[0]; B1 = IR_OP[1]; B2 = IR_OP[2];
  //   B3 = IR_OP[3]; B4 = IR_OP[4]; B5 = IR_OP[5]; B6 = IR_OP[6]; B7 = IR_OP[7]; B8 = IR_OP[8]; B9 = IR_OP[9];
  //   B10 = IR_OP[10]; B11 = IR_OP[11]; I = IR_OP[15]; T1 = IR_Load

  // Notes on the sheet:
  //   ---------------------------------------------------------------------------------------------------------------------------------------------------------------------------------------------------------------------------------
  //   ---------------------------------------------------------------------------------------------------------------------------------------------------------------------------------------------------------------------------------
  //   ---------------------------------------------------------------------------------------------------------------------------------------------------------------------------------------------------------------------------------
  //   ---------------------------------------------------------------------------------------------------------------------------------------------------------------------------------------------------------------------------------
  //   ---------------------------------------------------------------------------------------------------------------------------------------------------------------------------------------------------------------------------------
  //   ---------------------------------------------------------------------------------------------------------------------------------------------------------------------------------------------------------------------------------
  //   ---------------------------------------------------------------------------------------------------------------------------------------------------------------------------------------------------------------------------------
  //   ---------------------------------------------------------------------------------------------------------------------------------------------------------------------------------------------------------------------------------
endmodule

module SEQUNCE_COUNTER (
  input  CLK,
  input  CLR,
  output [2:0] OP
);

  wire [2:0] adder_1_out, multiplexer_1_out;

  Adder #(.width(3)) adder_1 (.a(OP), .b(3'b001), .out(adder_1_out));  // open: cin, cout
  Multiplexer #(.width(3)) multiplexer_1 (.in0(adder_1_out), .in1(3'b000), .out(multiplexer_1_out), .sel(CLR));
  Register #(.width(3)) register_1 (.D(multiplexer_1_out), .clk(CLK), .Q(OP));  // open: en, clr
endmodule
